# Fritzing sketch Plant_Watering_System_recover (saved by Fritzing 0.9.3b)
circuit board: 8.46667cm x 5.64444cm
breadboards: 1

parts:
  Part4 = FC-28 Soil Hygrometer Module
  Part5 = FC-28 Soil Hygrometer Module - Probe
  Componente1 = Arduino Uno (Rev3) - ICSP
  LED2 = LED - 5mm [color="Green (570nm)" package="5 mm [THT]"]
  LED3 = LED - 5mm [color="Red (633nm)" package="5 mm [THT]"]
  R1 = Resistor [tolerance=±5% resistance=220 package=THT]
  R2 = Resistor [tolerance=±5% resistance=220 package=THT]
  R3 = Resistor [tolerance=±5% resistance=220 package=THT]
  M1 = DC Motor

nets:
  VCC: Part4.VCC, Componente1.5V
  GND: Part4.GND, Componente1.GND, R2.Pin_1, R3.Pin_1, M1.pin_1
  N1: Part4.AO, Componente1.A0
  N2: Part4.POS, Part5.POS
  N3: Part4.NEG, Part5.NEG
  N4: Componente1.D4, LED3.anode
  N5: Componente1.D5_PWM, LED2.anode
  N6: Componente1.D6_PWM, R1.Pin_0
  N7: LED2.cathode, R2.Pin_0
  N8: LED3.cathode, R3.Pin_0
  N9: R1.Pin_1, M1.pin_2

notes:
  Esse motor simboliza a bomba d'água
  Sensor de nível de umidade do solo.

custom parts:
  FC-28 Soil Hygrometer Module: The FC-28 is a soil hygrometer module that uses the Texas Instruments LM393 comparator chip to provide an analog measurement of soil humidity. The digital output is high when soil moisture is over a certain threshold, as determined by adjusting the potentiometer.
  FC-28 Soil Hygrometer Module - Probe: The FC-28 is a soil hygrometer module that uses the Texas Instruments LM393 comparator chip to provide an analog measurement of soil humidity.
